# Fritzing sketch Electrisch_Schema_MP3 (saved by Fritzing 0.8.7b)
breadboards: 2

parts:
  Onderdeel1 = Arduino Uno (Rev3)
  S1 = Pushbutton [package="[THT]"]
  S2 = Pushbutton [package="[THT]"]
  R1 = Resistor [tolerance=±5% resistance=220 package=THT]
  R2 = Resistor [tolerance=±5% resistance=220 package=THT]
  U1 = POT [package=pot_alpha_rv16af-20]
  R3 = Photocell (LDR) [package=THT]
  R4 = Resistor [tolerance=±5% resistance=220 package=THT]
  J1 = Piezo Speaker
  7_Segment1 = 7 Segment Display
  R5 = Resistor [tolerance=±5% resistance=220 package=THT]
  R6 = Resistor [tolerance=±5% resistance=220 package=THT]
  R8 = Resistor [tolerance=±5% resistance=220 package=THT]
  R9 = Resistor [tolerance=±5% resistance=220 package=THT]
  R10 = Resistor [tolerance=±5% resistance=220 package=THT]
  R11 = Resistor [tolerance=±5% resistance=220 package=THT]
  R12 = Resistor [tolerance=±5% resistance=220 package=THT]
  LED1 = LED - 3mm [color="Red (633nm)" package="3 mm [THT]"]
  LED2 = LED - 3mm [color="Green (555nm)" package="3 mm [THT]"]
  R13 = Resistor [tolerance=±5% resistance=220 package=THT]
  R14 = Resistor [tolerance=±5% resistance=220 package=THT]
  R15 = Resistor [tolerance=±5% resistance=220 package=THT]

nets:
  N1: Onderdeel1.A0, U1.S
  N2: Onderdeel1.A1, R3.pin_0, R4.Pin_0
  N3: Onderdeel1.A2, R15.Pin_1
  N4: Onderdeel1.D8, R12.Pin_1
  N5: Onderdeel1.D9_PWM, R8.Pin_1
  N6: Onderdeel1.D10_PWM/SS, R9.Pin_1
  N7: Onderdeel1.D11_PWM/MOSI, LED2.anode
  N8: Onderdeel1.D12/MISO, LED1.anode
  N9: Onderdeel1.D2, S1.Pin_1, S1.Pin_2
  N10: Onderdeel1.D3_PWM, S2.Pin_1, S2.Pin_2, R1.Pin_0
  N11: Onderdeel1.D4, R6.Pin_1
  N12: Onderdeel1.D5_PWM, R5.Pin_1
  N13: Onderdeel1.D6_PWM, R10.Pin_1
  N14: Onderdeel1.D7, R11.Pin_1
  N15: Onderdeel1.5V, S1.Pin_3, S1.Pin_4, S2.Pin_3, S2.Pin_4, U1.A, R3.pin_1, J1.pin1
  N16: Onderdeel1.GND, R1.Pin_1, R2.Pin_1, U1.E, R4.Pin_1, 7_Segment1.common_anode, R13.Pin_0, R14.Pin_0
  N17: J1.pin2, R15.Pin_0
  N18: 7_Segment1.Segment_E, R12.Pin_0
  N19: 7_Segment1.Segment_D, R11.Pin_0
  N20: 7_Segment1.Segment_C, R10.Pin_0
  N21: 7_Segment1.Segment_B, R5.Pin_0
  N22: 7_Segment1.Segment_A, R6.Pin_0
  N23: 7_Segment1.Segment_F, R8.Pin_0
  N24: 7_Segment1.Segment_G, R9.Pin_0
  N25: LED1.cathode, R13.Pin_1
  N26: LED2.cathode, R14.Pin_1
